// Logisim project control_logic.circ as structural Verilog: 1 circuit, main circuit control_logic
module control_logic (
  input  [31:0] inst,
  input  BrEq,
  input  BrLt,
  output PCSel,
  output RegWEn,
  output [2:0] ImmSel,
  output BrUn,
  output ASel,
  output BSel,
  output [3:0] ALUSel,
  output MemRW,
  output [1:0] WBSel,
  output CSRSel,
  output CSRWen
);

  wire and1, and_2_out, and_3_out, and_4_out, and_5_out, and_6_out, and_7_out, comparator_2_eq,
       comparator_3_eq, comparator_5_eq, comparator_6_eq, comparator_7_eq, comparator_9_eq, comparator_10_eq,
       comparator_13_eq, comparator_14_eq, comparator_16_eq, comparator_17_eq, comparator_18_eq,
       comparator_19_eq, comparator_20_eq, comparator_21_eq, comparator_22_eq, comparator_23_eq,
       comparator_24_eq, comparator_25_eq, comparator_26_eq, comparator_27_eq, comparator_28_eq,
       comparator_29_eq, comparator_30_eq, comparator_31_eq, comparator_32_eq, comparator_33_eq,
       comparator_34_eq, comparator_35_eq, comparator_36_eq, comparator_37_eq, comparator_38_eq,
       comparator_39_eq, comparator_40_eq, comparator_41_eq, comparator_42_eq, comparator_43_eq,
       comparator_44_eq, comparator_45_eq, comparator_46_eq, comparator_47_eq, comparator_48_eq, divu8,
       I_type, mul10, mulh14, mulhu11, not_1_out, not_2_out, not_3_out, or2, or_5_out, or_6_out, or_8_out,
       or_9_out, or_10_out, or_11_out, or_12_out, or_16_out, or_17_out, R_type, reum9, SB_type, sll6, slt7,
       sra5, srl4, sub12, U_type, UJ_type, WBSel_alu, WBSel_lui, WBSel_pc, xor3;
  wire [1:0] multiplexer_1_out, multiplexer_3_out;
  wire [2:0] multiplexer_2_out, multiplexer_4_out, multiplexer_6_out, multiplexer_7_out, multiplexer_8_out;
  wire [3:0] multiplexer_9_out, multiplexer_11_out, multiplexer_12_out, multiplexer_13_out,
       multiplexer_14_out, multiplexer_15_out, multiplexer_16_out, multiplexer_17_out, multiplexer_18_out,
       multiplexer_19_out, multiplexer_20_out, multiplexer_21_out;

  Comparator #(.width(7)) comparator_1 (.a(inst[6:0]), .b(7'b0110111), .eq(WBSel_lui));  // open: gt, lt
  Comparator #(.width(7)) comparator_2 (.a(inst[6:0]), .b(7'b0010011), .eq(comparator_2_eq));  // open: gt, lt
  Comparator #(.width(7)) comparator_3 (.a(inst[6:0]), .b(7'b1100111), .eq(comparator_3_eq));  // open: gt, lt
  Multiplexer #(.enable("false"), .width(2)) multiplexer_1 (
    .in0(2'b00), .in1(2'b01), .out(multiplexer_1_out), .sel(WBSel_alu));
  Multiplexer #(.enable("false"), .width(3)) multiplexer_2 (
    .in0(3'b000), .in1(3'b000), .out(multiplexer_2_out), .sel(I_type));
  Comparator #(.width(7)) comparator_4 (.a(inst[6:0]), .b(7'b0110011), .eq(R_type));  // open: gt, lt
  Comparator #(.width(7)) comparator_5 (.a(inst[6:0]), .b(7'b1100111), .eq(comparator_5_eq));  // open: gt, lt
  Comparator #(.width(7)) comparator_6 (.a(inst[6:0]), .b(7'b0000011), .eq(comparator_6_eq));  // open: gt, lt
  Comparator #(.width(7)) comparator_7 (.a(inst[6:0]), .b(7'b0010011), .eq(comparator_7_eq));  // open: gt, lt
  Comparator #(.width(7)) comparator_8 (.a(inst[6:0]), .b(7'b0100011), .eq(MemRW));  // open: gt, lt
  Comparator #(.width(7)) comparator_9 (.a(inst[6:0]), .b(7'b0110111), .eq(comparator_9_eq));  // open: gt, lt
  Comparator #(.width(7)) comparator_10 (.a(inst[6:0]), .b(7'b0010111), .eq(comparator_10_eq));  // open: gt, lt
  Comparator #(.width(7)) comparator_11 (.a(inst[6:0]), .b(7'b1100011), .eq(SB_type));  // open: gt, lt
  Comparator #(.width(7)) comparator_12 (.a(inst[6:0]), .b(7'b1101111), .eq(UJ_type));  // open: gt, lt
  Comparator #(.width(7)) comparator_13 (.a(inst[6:0]), .b(7'b1110011), .eq(comparator_13_eq));  // open: gt, lt
  Comparator #(.width(3)) comparator_14 (.a(inst[14:12]), .b(3'b101), .eq(comparator_14_eq));  // open: gt, lt
  Comparator #(.width(7)) comparator_15 (.a(inst[6:0]), .b(7'b1110011), .eq(CSRWen));  // open: gt, lt
  or or_1 (WBSel_alu, R_type, comparator_2_eq, U_type);
  or or_2 (WBSel_pc, UJ_type, comparator_3_eq);
  Multiplexer #(.enable("false"), .width(2)) multiplexer_3 (
    .in0(multiplexer_1_out), .in1(2'b10), .out(multiplexer_3_out), .sel(WBSel_pc));
  Multiplexer #(.enable("false"), .width(3)) multiplexer_4 (
    .in0(multiplexer_2_out), .in1(3'b001), .out(multiplexer_4_out), .sel(MemRW));
  or or_3 (I_type, comparator_5_eq, comparator_6_eq, comparator_7_eq);
  or or_4 (U_type, comparator_9_eq, comparator_10_eq);
  and and_1 (CSRSel, comparator_13_eq, comparator_14_eq);
  Multiplexer #(.enable("false"), .width(2)) multiplexer_5 (
    .in0(multiplexer_3_out), .in1(2'b11), .out(WBSel), .sel(WBSel_lui));
  Multiplexer #(.enable("false"), .width(3)) multiplexer_6 (
    .in0(multiplexer_4_out), .in1(3'b010), .out(multiplexer_6_out), .sel(SB_type));
  Multiplexer #(.enable("false"), .width(3)) multiplexer_7 (
    .in0(multiplexer_6_out), .in1(3'b011), .out(multiplexer_7_out), .sel(U_type));
  Multiplexer #(.enable("false"), .width(3)) multiplexer_8 (
    .in0(multiplexer_7_out), .in1(3'b100), .out(multiplexer_8_out), .sel(UJ_type));
  Comparator #(.width(7)) comparator_16 (.a(inst[6:0]), .b(7'b0010011), .eq(comparator_16_eq));  // open: gt, lt
  Multiplexer #(.enable("false"), .width(4)) multiplexer_9 (
    .in0(4'b0000), .in1(4'b0001), .out(multiplexer_9_out), .sel(and1));
  Comparator #(.width(3)) comparator_17 (.a(inst[14:12]), .b(3'b001), .eq(comparator_17_eq));  // open: gt, lt
  not not_1 (not_1_out, BrEq);
  Comparator #(.width(3)) comparator_18 (.a(inst[14:12]), .b(3'b100), .eq(comparator_18_eq));  // open: gt, lt
  Comparator #(.width(3)) comparator_19 (.a(inst[14:12]), .b(3'b101), .eq(comparator_19_eq));  // open: gt, lt
  not not_2 (not_2_out, BrLt);
  Comparator #(.width(3)) comparator_20 (.a(inst[14:12]), .b(3'b110), .eq(comparator_20_eq));  // open: gt, lt
  Comparator #(.width(3)) comparator_21 (.a(inst[14:12]), .b(3'b111), .eq(comparator_21_eq));  // open: gt, lt
  not not_3 (not_3_out, BrLt);
  Multiplexer #(.enable("false"), .width(3)) multiplexer_10 (
    .in0(multiplexer_8_out), .in1(3'b101), .out(ImmSel), .sel(CSRSel));
  Multiplexer #(.enable("false"), .width(4)) multiplexer_11 (
    .in0(multiplexer_9_out), .in1(4'b0010), .out(multiplexer_11_out), .sel(or2));
  Comparator #(.width(3)) comparator_22 (.a(inst[14:12]), .b(3'b000), .eq(comparator_22_eq));  // open: gt, lt
  and and_2 (and_2_out, SB_type, comparator_17_eq, not_1_out);
  and and_3 (and_3_out, SB_type, comparator_18_eq, BrLt);
  and and_4 (and_4_out, SB_type, comparator_19_eq, not_2_out);
  and and_5 (and_5_out, SB_type, comparator_20_eq, BrLt);
  and and_6 (and_6_out, SB_type, comparator_21_eq, not_3_out);
  Comparator #(.width(7)) comparator_23 (.a(inst[31:25]), .b(7'b0000001), .eq(comparator_23_eq));  // open: gt, lt
  Comparator #(.width(3)) comparator_24 (.a(inst[14:12]), .b(3'b000), .eq(comparator_24_eq));  // open: gt, lt
  Comparator #(.width(7)) comparator_25 (.a(inst[31:25]), .b(7'b0100000), .eq(comparator_25_eq));  // open: gt, lt
  Comparator #(.width(3)) comparator_26 (.a(inst[14:12]), .b(3'b000), .eq(comparator_26_eq));  // open: gt, lt
  Comparator #(.width(7)) comparator_27 (.a(inst[31:25]), .b({7{1'b0}}), .eq(comparator_27_eq));  // open: gt, lt
  Comparator #(.width(3)) comparator_28 (.a(inst[14:12]), .b(3'b001), .eq(comparator_28_eq));  // open: gt, lt
  Comparator #(.width(7)) comparator_29 (.a(inst[31:25]), .b(7'b0000001), .eq(comparator_29_eq));  // open: gt, lt
  Comparator #(.width(3)) comparator_30 (.a(inst[14:12]), .b(3'b001), .eq(comparator_30_eq));  // open: gt, lt
  Comparator #(.width(7)) comparator_31 (.a(inst[31:25]), .b(7'b0000001), .eq(comparator_31_eq));  // open: gt, lt
  Comparator #(.width(3)) comparator_32 (.a(inst[14:12]), .b(3'b011), .eq(comparator_32_eq));  // open: gt, lt
  or or_5 (or_5_out, R_type, comparator_16_eq);
  Comparator #(.width(3)) comparator_33 (.a(inst[14:12]), .b(3'b010), .eq(comparator_33_eq));  // open: gt, lt
  or or_6 (or_6_out, R_type, I_type);
  Comparator #(.width(3)) comparator_34 (.a(inst[14:12]), .b(3'b100), .eq(comparator_34_eq));  // open: gt, lt
  Multiplexer #(.enable("false"), .width(4)) multiplexer_12 (
    .in0(multiplexer_11_out), .in1(4'b0011), .out(multiplexer_12_out), .sel(xor3));
  or or_7 (RegWEn, R_type, I_type, UJ_type, U_type);
  and and_7 (and_7_out, SB_type, comparator_22_eq, BrEq);
  or or_8 (or_8_out, R_type, I_type);
  and and_8 (xor3, or_6_out, comparator_34_eq);
  Multiplexer #(.enable("false"), .width(4)) multiplexer_13 (
    .in0(multiplexer_12_out), .in1(4'b0100), .out(multiplexer_13_out), .sel(srl4));
  and and_9 (mul10, comparator_23_eq, comparator_24_eq, R_type);
  and and_10 (sub12, comparator_25_eq, comparator_26_eq, R_type);
  and and_11 (sll6, comparator_27_eq, comparator_28_eq, or_8_out);
  and and_12 (mulh14, comparator_29_eq, comparator_30_eq, R_type);
  and and_13 (mulhu11, comparator_31_eq, comparator_32_eq, R_type);
  and and_14 (slt7, or_5_out, comparator_33_eq);
  Multiplexer #(.enable("false"), .width(4)) multiplexer_14 (
    .in0(multiplexer_13_out), .in1(4'b0101), .out(multiplexer_14_out), .sel(sra5));
  or or_9 (or_9_out, and_7_out, and_2_out, and_3_out, and_4_out, and_5_out, and_6_out);
  Multiplexer #(.enable("false"), .width(4)) multiplexer_15 (
    .in0(multiplexer_14_out), .in1(4'b0110), .out(multiplexer_15_out), .sel(sll6));
  Comparator #(.width(7)) comparator_35 (.a(inst[6:0]), .b(7'b0010111), .eq(comparator_35_eq));  // open: gt, lt
  Multiplexer #(.enable("false"), .width(4)) multiplexer_16 (
    .in0(multiplexer_15_out), .in1(4'b0111), .out(multiplexer_16_out), .sel(slt7));
  Comparator #(.width(7)) comparator_36 (.a(inst[6:0]), .b(7'b1100111), .eq(comparator_36_eq));  // open: gt, lt
  Comparator #(.width(7)) comparator_37 (.a(inst[31:25]), .b(7'b0000001), .eq(comparator_37_eq));  // open: gt, lt
  Comparator #(.width(3)) comparator_38 (.a(inst[14:12]), .b(3'b101), .eq(comparator_38_eq));  // open: gt, lt
  Comparator #(.width(7)) comparator_39 (.a(inst[31:25]), .b({7{1'b0}}), .eq(comparator_39_eq));  // open: gt, lt
  Comparator #(.width(3)) comparator_40 (.a(inst[14:12]), .b(3'b101), .eq(comparator_40_eq));  // open: gt, lt
  Comparator #(.width(7)) comparator_41 (.a(inst[31:25]), .b(7'b0100000), .eq(comparator_41_eq));  // open: gt, lt
  Comparator #(.width(3)) comparator_42 (.a(inst[14:12]), .b(3'b101), .eq(comparator_42_eq));  // open: gt, lt
  or or_10 (or_10_out, R_type, I_type);
  or or_11 (or_11_out, R_type, I_type);
  Comparator #(.width(3)) comparator_43 (.a(inst[14:12]), .b(3'b110), .eq(comparator_43_eq));  // open: gt, lt
  Comparator #(.width(7)) comparator_44 (.a(inst[31:25]), .b(7'b0000001), .eq(comparator_44_eq));  // open: gt, lt
  Comparator #(.width(3)) comparator_45 (.a(inst[14:12]), .b(3'b111), .eq(comparator_45_eq));  // open: gt, lt
  or or_12 (or_12_out, R_type, I_type);
  Comparator #(.width(3)) comparator_46 (.a(inst[14:12]), .b(3'b111), .eq(comparator_46_eq));  // open: gt, lt
  Multiplexer #(.enable("false"), .width(4)) multiplexer_17 (
    .in0(multiplexer_16_out), .in1(4'b1000), .out(multiplexer_17_out), .sel(divu8));
  Multiplexer #(.enable("false"), .width(4)) multiplexer_18 (
    .in0(multiplexer_17_out), .in1(4'b1001), .out(multiplexer_18_out), .sel(reum9));
  Comparator #(.width(3)) comparator_47 (.a(inst[14:12]), .b(3'b110), .eq(comparator_47_eq));  // open: gt, lt
  Comparator #(.width(3)) comparator_48 (.a(inst[14:12]), .b(3'b111), .eq(comparator_48_eq));  // open: gt, lt
  or or_13 (PCSel, or_9_out, UJ_type, comparator_36_eq);
  or or_14 (ASel, SB_type, comparator_35_eq, UJ_type);
  or or_15 (BSel, I_type, U_type, MemRW, SB_type, UJ_type);
  or or_16 (or_16_out, R_type, I_type);
  and and_15 (or2, or_11_out, comparator_43_eq);
  and and_16 (reum9, comparator_44_eq, comparator_45_eq, R_type);
  and and_17 (and1, or_12_out, comparator_46_eq);
  Multiplexer #(.enable("false"), .width(4)) multiplexer_19 (
    .in0(multiplexer_18_out), .in1(4'b1010), .out(multiplexer_19_out), .sel(mul10));
  or or_17 (or_17_out, comparator_47_eq, comparator_48_eq);
  and and_18 (divu8, comparator_37_eq, comparator_38_eq, R_type);
  and and_19 (srl4, comparator_39_eq, comparator_40_eq, or_16_out);
  and and_20 (sra5, comparator_41_eq, comparator_42_eq, or_10_out);
  Multiplexer #(.enable("false"), .width(4)) multiplexer_20 (
    .in0(multiplexer_19_out), .in1(4'b1011), .out(multiplexer_20_out), .sel(mulhu11));
  and and_21 (BrUn, SB_type, or_17_out);
  Multiplexer #(.enable("false"), .width(4)) multiplexer_21 (
    .in0(multiplexer_20_out), .in1(4'b1100), .out(multiplexer_21_out), .sel(sub12));
  Multiplexer #(.enable("false"), .width(4)) multiplexer_22 (
    .in0(multiplexer_21_out), .in1(4'b1110), .out(ALUSel), .sel(mulh14));

  // Other names for the same wires on the sheet: CSRRWI_type = CSRSel; Opcode[6:0] = inst[6:0]; rd[4:0] = inst[11:7];
  //   funct3[2:0] = inst[14:12]; rs1[4:0] = inst[19:15]; rs2[4:0] = inst[24:20]; funct7[6:0] = inst[31:25];
  //   S_type = MemRW

  // Notes on the sheet:
  //   INPUTS to your circuit
  //   DON'T CHANGE THE LOCATIONS OF THE INPUTS AND OUTPUTS!
  //   OUTPUT from your circuit
endmodule
