// Logisim project cpu.circ as structural Verilog: 1 circuit, main circuit cpu
module cpu (
  input  clk,
  input  [31:0] INSTRUCTION,
  input  [31:0] READ_DATA,
  output [31:0] WRITE_ADDRESS,
  output [31:0] PROGRAM_COUNTER,
  output [31:0] ra,
  output [31:0] sp,
  output [31:0] t0,
  output [31:0] t1,
  output [31:0] t2,
  output [31:0] s0,
  output [31:0] s1,
  output [31:0] a0,
  output [31:0] tohost,
  output [3:0] WRITE_ENABLE,
  output [31:0] WRITE_DATA
);

  wire ASel, BrEq, BrLt, BrUn, BSel, comparator_1_eq, comparator_2_eq, comparator_3_eq, comparator_4_eq,
       CSRSel, CSRWen, lb, lh, MemRW, PCSel, RegWEn;
  wire [1:0] WBSel;
  wire [2:0] fun3, ImmSel;
  wire [3:0] ALUSel;
  wire [6:0] fun7;
  wire [24:0] INSTRUCTION2;
  wire [31:0] adder_1_out, adder_2_out, bit_extender_2_out, bit_extender_3_out, imm, multiplexer_1_out,
       multiplexer_2_out, multiplexer_3_out, multiplexer_4_out, multiplexer_5_out, multiplexer_7_out,
       PROGRAM_COUNTER2, r1, READ_DATA2, result;

  Adder #(.width(32)) adder_1 (.a(PROGRAM_COUNTER), .b(32'h4), .out(adder_1_out));  // open: cin, cout
  Multiplexer #(.enable("false"), .width(32)) multiplexer_1 (
    .in0(adder_1_out), .in1(WRITE_ADDRESS), .out(multiplexer_1_out), .sel(PCSel));
  Register #(.width(32)) PC (.D(multiplexer_1_out), .clk(clk), .Q(PROGRAM_COUNTER));  // open: en, clr
  Multiplexer #(.enable("false"), .width(32)) multiplexer_2 (
    .in0(INSTRUCTION), .in1(32'h13), .out(multiplexer_2_out), .sel(PCSel));
  Register #(.width(32)) register_1 (.D(PROGRAM_COUNTER), .clk(clk), .Q(PROGRAM_COUNTER2));  // open: en, clr
  Register #(.width(32)) register_2 (
    .D(multiplexer_2_out), .clk(clk), .Q({fun7, INSTRUCTION2[24:15], fun3, INSTRUCTION2[11:0]}));  // open: en, clr
  Comparator #(.width(7)) comparator_1 (.a(INSTRUCTION2[6:0]), .b(7'b0000011), .eq(comparator_1_eq));  // open: gt, lt
  Comparator #(.width(3)) comparator_2 (.a(fun3), .b(3'b000), .eq(comparator_2_eq));  // open: gt, lt
  Comparator #(.width(7)) comparator_3 (.a(INSTRUCTION2[6:0]), .b(7'b0000011), .eq(comparator_3_eq));  // open: gt, lt
  Comparator #(.width(3)) comparator_4 (.a(fun3), .b(3'b001), .eq(comparator_4_eq));  // open: gt, lt
  imm_gen imm_gen_1 (.inst({fun7, INSTRUCTION2[24:15], fun3, INSTRUCTION2[11:0]}), .ImmSel(ImmSel), .imm(imm));
  and and_1 (lb, comparator_1_eq, comparator_2_eq);
  and and_2 (lh, comparator_3_eq, comparator_4_eq);
  control_logic control_logic_1 (
    .CSRWen(CSRWen), .PCSel(PCSel), .RegWEn(RegWEn), .ImmSel(ImmSel), .BrUn(BrUn), .ASel(ASel), .BSel(BSel),
    .ALUSel(ALUSel), .MemRW(MemRW), .WBSel(WBSel), .CSRSel(CSRSel),
    .inst({fun7, INSTRUCTION2[24:15], fun3, INSTRUCTION2[11:0]}), .BrEq(BrEq), .BrLt(BrLt));
  regfile regfile_1 (
    .rs1(INSTRUCTION2[19:15]), .rs2(INSTRUCTION2[24:20]), .rd(INSTRUCTION2[11:7]), .Write_Data(result),
    .RegWEn(RegWEn), .clk(clk), .ra(ra), .sp(sp), .t0(t0), .t1(t1), .t2(t2), .s0(s0), .s1(s1), .a0(a0),
    .Read_Data_1(r1), .Read_Data_2(WRITE_DATA));
  branch_comp branch_comp_1 (.rs1(r1), .rs2(WRITE_DATA), .BrUn(BrUn), .BrEq(BrEq), .BrLt(BrLt));
  Multiplexer #(.enable("false"), .width(32)) multiplexer_3 (
    .in0(r1), .in1(imm), .out(multiplexer_3_out), .sel(CSRSel));
  Multiplexer #(.enable("false"), .width(32)) multiplexer_4 (
    .in0(r1), .in1(PROGRAM_COUNTER2), .out(multiplexer_4_out), .sel(ASel));
  Multiplexer #(.enable("false"), .width(32)) multiplexer_5 (
    .in0(WRITE_DATA), .in1(imm), .out(multiplexer_5_out), .sel(BSel));
  alu alu_1 (.Result(WRITE_ADDRESS), .A(multiplexer_4_out), .B(multiplexer_5_out), .ALUSel(ALUSel));
  csr csr_1 (.CSR_address(12'h51e), .CSR_din(multiplexer_3_out), .CSR_WE(CSRWen), .clk(clk), .tohost(tohost));
  Adder #(.width(32)) adder_2 (.a(32'h4), .b(PROGRAM_COUNTER2), .out(adder_2_out));  // open: cin, cout
  Multiplexer #(.enable("false"), .select(2), .width(32)) multiplexer_6 (
    .in0(READ_DATA2), .in1(WRITE_ADDRESS), .in2(adder_2_out), .in3(imm), .out(result), .sel(WBSel));
  assign WRITE_ENABLE = {{3{MemRW}}, MemRW};  // Bit_Extender bit_extender_1
  assign bit_extender_2_out = {{24{READ_DATA[7]}}, READ_DATA[7:0]};  // Bit_Extender bit_extender_2
  assign bit_extender_3_out = {{16{READ_DATA[15]}}, READ_DATA[15:0]};  // Bit_Extender bit_extender_3
  Multiplexer #(.enable("false"), .width(32)) multiplexer_7 (
    .in0(READ_DATA), .in1(bit_extender_3_out), .out(multiplexer_7_out), .sel(lh));
  Multiplexer #(.enable("false"), .width(32)) multiplexer_8 (
    .in0(multiplexer_7_out), .in1(bit_extender_2_out), .out(READ_DATA2), .sel(lb));

  // Other names for the same wires on the sheet: ALU_output[31:0] = WRITE_ADDRESS; Opcode[6:0] = INSTRUCTION2[6:0];
  //   rd[4:0] = INSTRUCTION2[11:7]; INSTRUCTION2 (some bits) = {fun7, fun3}; rs1[4:0] = INSTRUCTION2[19:15];
  //   rs2[4:0] = INSTRUCTION2[24:20]; r2[31:0] = WRITE_DATA

  // Notes on the sheet:
  //   Output to IMEM
  //   IMEM (do **NOT** move this)
  //   Inputs from IMEM
  //   It is OK to move the PC, RegFile, ALU, MEM, Branch Comp, Imm Gen, and Control Logic to wherever is most convenient for you when constructing your CPU, and to delete this text
  //   Inputs/Outputs for testing. Do **NOT** move these.
  //   Outputs To DMEM
  //   DMEM (do **NOT** move this)
  //   Inputs From DMEM
endmodule
